# Fritzing sketch lifi (saved by Fritzing 0.9.3b)
breadboards: 1

parts:
  Part1 = Arduino Uno (Rev3)
  LED2 = LED - 5mm [color="Red (633nm)" package="5 mm [THT]"]
  LED3 = LED - 5mm [color="Red (633nm)" package="5 mm [THT]"]
  Part2 = Arduino Uno (Rev3)
  R1 = Resistor [tolerance=±5% resistance=10 package=THT]
  R2 = Resistor [tolerance=±5% resistance=10 package=THT]
  R3 = Resistor [tolerance=±5% resistance=10k package=THT]

nets:
  N1: Part1.GND, LED2.cathode
  N2: LED3.cathode, Part2.D2, R3.Pin_0
  N3: LED3.anode, Part2.5V
  N4: Part2.GND, R1.Pin_1
  N5: R1.Pin_0, R2.Pin_1
  N6: R2.Pin_0, R3.Pin_1
